# Fritzing sketch donkeybounceshield-old (saved by Fritzing 0.9.3b)
circuit board: 6.88566cm x 5.36311cm
breadboards: 1

parts:
  Part1 = Arduino Uno (Rev3) - ICSP
  GPS-08975 = mystery part, 5 pins [chip_label=GPS-08975 part_number=LS20031]
  Throttle = mystery part, 3 pins [chip_label=Throttle-OUT]
  U3 = mystery part, 3 pins [chip_label=Steering-IN]
  Steering = mystery part, 3 pins [chip_label=Steering-OUT]
  Part2 = InvenSense MPU6050
  U6 = mystery part, 3 pins [chip_label=Throttle-IN]
  HC-SR04 = HC-SR04 Ultrasonic Distance Sensor

nets:
  N1: Part1.A0, HC-SR04.TRIG
  N2: Part1.A1, HC-SR04.ECHO
  N3: Part1.A2, Throttle.pin3, U6.pin3
  N4: Part1.A3, U3.pin3, Steering.pin3
  N5: Part1.A4/SDA, Part2.SDA
  N6: Part1.A5/SCL, Part2.SCL
  GND: Part1.GND, GPS-08975.pin1, Throttle.pin1, U3.pin1, Steering.pin1, Part2.GND, U6.pin1, HC-SR04.GND
  N7: Part1.D4, GPS-08975.pin3
  N8: Part1.3V3, GPS-08975.pin5
  VCC: Part1.5V, Part2.VCC, HC-SR04.VCC
  N9: Throttle.pin2, U6.pin2
  N10: U3.pin2, Steering.pin2

notes:
  DKL - 2019
  Donkey Bounce Car

custom parts:
  HC-SR04 Ultrasonic Distance Sensor: The HC-SR04 is an ultrasonic distance sensor. It is capable of providing measurement for ranges of 2cm to 400cm. The module operates at 5V.
