# Fritzing sketch donkeybounceshield-v2 (saved by Fritzing 0.9.3b)
circuit board: 6.88566cm x 5.36311cm
breadboards: 1

parts:
  Part1 = Arduino Uno (Rev3)
  U5 = XC2C64A [package=tqfp44]
  GPS-8977 = mystery part, 5 pins [chip_label=GPS-08975 part_number=LS20031]
  HC-SR5 = HC-SR04 Ultrasonic Distance Sensor
  Th-Out = mystery part, 3 pins [chip_label=Throttle-OUT]
  St-Out = mystery part, 3 pins [chip_label=Steering-OUT]
  GPS-8978 = mystery part, 6 pins [chip_label=JTAG]
  St-In = mystery part, 3 pins [chip_label=Steering-OUT]
  Th-In = mystery part, 3 pins [chip_label=Throttle-OUT]
  C1 = Capacitor [package=1206]
  C2 = Capacitor [package=1206]
  C4 = Capacitor [package=1206]
  C5 = Capacitor [package=1206]
  C6 = Capacitor [package=1206]
  SJ3 = Solder Jumper [package=sj_3]
  SJ4 = Solder Jumper [package=sj_3]
  SJ5 = Solder Jumper [package=sj_3]
  SJ2 = Solder Jumper [package=sj_3]
  Q6 = MOSFET-NCHANNEL [package=sot23-3]
  Q7 = MOSFET-NCHANNEL [package=sot23-3]
  Q8 = MOSFET-NCHANNEL [package=sot23-3]
  Q9 = MOSFET-NCHANNEL [package=sot23-3]
  U7 = MTK3339 [package="custom, 16x16mm"]
  LED1 = smd LED [color="Red (633nm)" package="0603 [SMD]"]
  C7 = Capacitor [package=1206]
  SJ6 = Solder Jumper [package=sj_2s-no]
  SJ7 = Solder Jumper [package=sj_2s-no]
  SJ8 = Solder Jumper [package=sj_2s-no]
  U6 = Voltage Regulator LDO [package=sot23-5]
  R9 = Resistor [tolerance=±5% resistance=1k package="0603 [SMD]"]
  R10 = Resistor [tolerance=±5% resistance=10k package="0603 [SMD]"]
  R7 = Resistor [tolerance=±5% resistance=10k package="0603 [SMD]"]
  R8 = Resistor [tolerance=±5% resistance=10k package="0603 [SMD]"]
  R3 = Resistor [tolerance=±5% resistance=10k package="0603 [SMD]"]
  R4 = Resistor [tolerance=±5% resistance=10k package="0603 [SMD]"]
  R2 = Resistor [tolerance=±5% resistance=10k package="0603 [SMD]"]
  R6 = Resistor [tolerance=±5% resistance=10k package="0603 [SMD]"]
  R5 = Resistor [tolerance=±5% resistance=10k package="0603 [SMD]"]
  R1 = Resistor [tolerance=±5% resistance=10k package="0603 [SMD]"]
  D2 = Diode [package=diode-1n4148]
  C3 = Capacitor [package=1206]
  GPS-8979 = mystery part, 6 pins [chip_label=JTAG]
  Part3 = InvenSense MPU6050

nets:
  N1: Part1.A0, HC-SR5.ECHO
  N2: Part1.A1, HC-SR5.TRIG
  N3: Part1.A4/SDA, GPS-8979.pin4, Part3.SDA
  N4: Part1.A5/SCL, GPS-8979.pin5, Part3.SCL
  N5: Part1.D9_PWM, Th-Out.pin1
  N6: Part1.D10_PWM/SS, St-Out.pin1
  N7: Part1.D11_PWM/MOSI, Q8.D, R5.Pin_0
  N8: Part1.D12/MISO, U5.IO_15
  N9: Part1.D13/SCK, Q7.D, R2.Pin_0
  GND: Part1.GND, U5.GND, GPS-8977.pin1, GPS-8977.pin2, HC-SR5.GND, Th-Out.pin3, St-Out.pin3, GPS-8978.pin2, St-In.pin3, Th-In.pin3, C1.2, C2.1, C4.1, C5.1, C6.1, U7.GND, C7.1, U6.GND, R9.Pin_1, C3.1, GPS-8979.pin3, Part3.GND
  N10: Part1.D3_PWM, D2.C
  N11: Part1.D4, GPS-8977.pin3, U7.TX, SJ7.1, SJ7.2
  3V3: Part1.3V3, U5.VDDIO1, U5.VDDIO2, U5.VDDAUX, GPS-8977.pin5, GPS-8978.pin1, C1.1, C4.2, C6.2, U7.VCC, C7.2, SJ6.1, SJ6.2, U6.IN, U6.EN, R10.Pin_1, C3.2
  VCC: Part1.5V, HC-SR5.VCC, SJ3.1, SJ3.2, SJ4.2, SJ4.3, SJ5.1, SJ5.2, SJ2.1, SJ2.2, Q6.G, Q7.G, Q8.G, Q9.G, R7.Pin_0, R3.Pin_0, R2.Pin_1, R5.Pin_1, GPS-8979.pin1, Part3.VCC
  N12: U5.IO_27, Q8.S, R1.Pin_0
  N13: U5.TDI, GPS-8978.pin5
  N14: U5.TMS, GPS-8978.pin6
  N15: U5.TCK, GPS-8978.pin3
  N16: U5.VDDINT, C2.2, C5.2, SJ3.3, SJ4.1, SJ5.3, SJ2.3, U6.OUT, R8.Pin_0, R4.Pin_0, R6.Pin_1, R1.Pin_1
  N17: U5.IO_32, Q7.S, R6.Pin_0
  N18: U5.TDO, GPS-8978.pin4
  N19: U5.IO_8, Q9.S, R4.Pin_1
  N20: U5.IO_17, Q6.S, R8.Pin_1
  N21: GPS-8977.pin4, U7.RX, SJ8.1, SJ8.2, R10.Pin_0, D2.A
  N22: Th-Out.pin2, Th-In.pin2
  N23: St-Out.pin2, St-In.pin2
  N24: St-In.pin1, Q6.D, R7.Pin_1
  N25: Th-In.pin1, Q9.D, R3.Pin_1
  N26: U7.3D-FIX, LED1.anode
  N27: LED1.cathode, R9.Pin_0

notes:
  3V3
  GND
  TCK
  TDO
  TDI
  TMS
  DKL - 2019
  Donkey Bounce Car

custom parts:
  XC2C64A: XC2C64A - Coolrunner II CPLD
  HC-SR04 Ultrasonic Distance Sensor: The HC-SR04 is an ultrasonic distance sensor. It is capable of providing measurement for ranges of 2cm to 400cm. The module operates at 5V.
  MTK3339: Ultimate GPS Module - 66 channel w/10 Hz updates (MTK3339 chipset)
